// Logisim project 01 - Combinational_Part - Using_Basic_Gates (Unsimplified_Form).circ as structural Verilog: 1 circuit, main circuit main
module main (
  input  X,
  input  Y,
  input  Z
);

  wire not_1_out, not_2_out, not_3_out, or_1_out, or_2_out, or_3_out, or_4_out, or_5_out, or_6_out, or_7_out,
       or_8_out, or_9_out, or_10_out, or_11_out, X_prime_Y_prime_Z_out, X_prime_Y_prime_Z_prime_out,
       X_prime_YZ_out, X_prime_YZ_prime_out, XY_prime_Z_out, XY_prime_Z_prime_out, XYZ_prime_out;

  not not_1 (not_1_out, X);
  not not_2 (not_2_out, Z);
  not not_3 (not_3_out, Y);
  and X_prime_Y_prime_Z_prime (X_prime_Y_prime_Z_prime_out, not_1_out, not_3_out, not_2_out);
  and X_prime_Y_prime_Z (X_prime_Y_prime_Z_out, not_1_out, not_3_out, Z);
  and X_prime_YZ_prime (X_prime_YZ_prime_out, not_1_out, Y, not_2_out);
  and X_prime_YZ (X_prime_YZ_out, not_1_out, Y, Z);
  and XY_prime_Z_prime (XY_prime_Z_prime_out, X, not_3_out, not_2_out);
  and XY_prime_Z (XY_prime_Z_out, X, not_3_out, Z);
  and XYZ_prime (XYZ_prime_out, X, Y, not_2_out);
  or or_1 (or_1_out, X_prime_Y_prime_Z_prime_out, X_prime_YZ_prime_out, XY_prime_Z_prime_out);
  or or_2 (or_2_out, X_prime_Y_prime_Z_prime_out, X_prime_YZ_prime_out, X_prime_YZ_out);
  or or_3 (or_3_out, or_1_out, XY_prime_Z_out);
  or or_4 (or_4_out, X_prime_Y_prime_Z_prime_out, X_prime_YZ_prime_out);
  or or_5 (or_5_out, or_2_out, XY_prime_Z_prime_out, XY_prime_Z_out);
  or or_6 (or_6_out, X_prime_Y_prime_Z_prime_out, X_prime_YZ_prime_out, X_prime_YZ_out);
  or or_7 (or_7_out, or_6_out, XY_prime_Z_prime_out);
  or or_8 (or_8_out, X_prime_Y_prime_Z_prime_out, X_prime_YZ_prime_out, XY_prime_Z_prime_out);
  or or_9 (or_9_out, or_8_out, XY_prime_Z_out);
  or or_10 (or_10_out, X_prime_Y_prime_Z_prime_out, X_prime_Y_prime_Z_out, X_prime_YZ_prime_out);
  or or_11 (or_11_out, or_10_out, XY_prime_Z_out);
  _7_Segment_Display u_7_segment_display_1 (
    .g(or_11_out), .f(or_9_out), .a(or_3_out), .b(or_4_out), .e(or_7_out), .d(or_5_out), .c(or_5_out),
    .dp(XYZ_prime_out));
endmodule
