// Logisim project 02 - Combinational_Part - Using_Basic_Gates.circ as structural Verilog: 1 circuit, main circuit main
module main (
  input  X,
  input  Y,
  input  Z
);

  wire A, and_1_out, and_2_out, and_3_out, and_4_out, and_5_out, and_6_out, and_7_out, and_8_out, and_9_out,
       and_10_out, and_11_out, B, C, DP, E, F, G, not_1_out, not_2_out, not_3_out, or_1_out;

  not not_1 (not_1_out, X);
  not not_2 (not_2_out, Y);
  not not_3 (not_3_out, Z);
  and and_1 (and_1_out, not_3_out, not_1_out);
  and and_2 (and_2_out, not_2_out, X);
  and and_3 (and_3_out, not_1_out, Y);
  and and_4 (and_4_out, X, not_2_out);
  and and_5 (and_5_out, not_2_out, not_3_out);
  and and_6 (and_6_out, not_1_out, Y);
  and and_7 (and_7_out, not_3_out, not_2_out);
  and and_8 (and_8_out, not_3_out, not_1_out);
  and and_9 (and_9_out, not_2_out, X);
  and and_10 (and_10_out, not_1_out, not_3_out);
  and and_11 (and_11_out, not_2_out, Z);
  or or_1 (or_1_out, and_3_out, and_4_out);
  or or_2 (A, and_1_out, and_2_out);
  and and_12 (B, not_1_out, not_3_out);
  or or_3 (C, or_1_out, and_5_out);
  or or_4 (E, and_6_out, and_7_out);
  or or_5 (F, and_8_out, and_9_out);
  or or_6 (G, and_10_out, and_11_out);
  and and_13 (DP, X, Y, not_3_out);
  _7_Segment_Display u_7_segment_display_1 (.g(G), .f(F), .a(A), .b(B), .e(E), .d(C), .c(C), .dp(DP));

  // Other names for the same wires on the sheet: D = C
endmodule
