// Logisim project 03 - Combinational_Part - Using_NAND_Gates.circ as structural Verilog: 1 circuit, main circuit main
module main (
  input  X,
  input  Y,
  input  Z
);

  wire A, B, C, DP, E, F, G, nand_1_out, nand_2_out, nand_3_out, nand_4_out, nand_5_out, nand_6_out,
       nand_7_out, nand_8_out, nand_9_out, nand_10_out, nand_11_out, nand_12_out, nand_13_out, nand_14_out,
       nand_15_out, nand_16_out;

  nand nand_1 (nand_1_out, X, X);
  nand nand_2 (nand_2_out, Z, Z);
  nand nand_3 (nand_3_out, Y, Y);
  nand nand_4 (nand_4_out, nand_1_out, nand_2_out);
  nand nand_5 (nand_5_out, X, nand_3_out);
  nand nand_6 (nand_6_out, nand_1_out, nand_2_out);
  nand nand_7 (nand_7_out, nand_1_out, Y);
  nand nand_8 (nand_8_out, X, nand_3_out);
  nand nand_9 (nand_9_out, nand_3_out, nand_2_out);
  nand nand_10 (nand_10_out, nand_1_out, Y);
  nand nand_11 (nand_11_out, nand_3_out, nand_2_out);
  nand nand_12 (nand_12_out, nand_1_out, nand_2_out);
  nand nand_13 (nand_13_out, X, nand_3_out);
  nand nand_14 (nand_14_out, nand_1_out, nand_2_out);
  nand nand_15 (nand_15_out, nand_3_out, Z);
  nand nand_16 (nand_16_out, X, Y, nand_2_out);
  nand nand_17 (A, nand_4_out, nand_5_out);
  nand nand_18 (B, nand_6_out, nand_6_out);
  nand nand_19 (C, nand_7_out, nand_8_out, nand_9_out);
  nand nand_20 (E, nand_10_out, nand_11_out);
  nand nand_21 (F, nand_12_out, nand_13_out);
  nand nand_22 (G, nand_14_out, nand_15_out);
  nand nand_23 (DP, nand_16_out, nand_16_out);
  _7_Segment_Display u_7_segment_display_1 (.g(G), .f(F), .a(A), .b(B), .e(E), .d(C), .c(C), .dp(DP));

  // Other names for the same wires on the sheet: D = C
endmodule
