// Logisim project 04 - Combinational_Part - Using_NOR_Gates.circ as structural Verilog: 1 circuit, main circuit main
module main (
  input  X,
  input  Y,
  input  Z
);

  wire a, b, c, dp, e, f, g, nor_1_out, nor_2_out, nor_3_out, nor_4_out, nor_5_out, nor_7_out, nor_8_out,
       nor_9_out, nor_10_out, nor_11_out, nor_12_out, nor_13_out, nor_14_out, nor_15_out, nor_17_out,
       nor_18_out, nor_19_out, nor_20_out, nor_21_out;

  nor nor_1 (nor_1_out, X, X);
  nor nor_2 (nor_2_out, Y, Y);
  nor nor_3 (nor_3_out, Z, Z);
  nor nor_4 (nor_4_out, X, Z);
  nor nor_5 (nor_5_out, nor_1_out, Y);
  nor nor_6 (b, X, Z);
  nor nor_7 (nor_7_out, X, nor_2_out);
  nor nor_8 (nor_8_out, nor_1_out, Y);
  nor nor_9 (nor_9_out, Y, Z);
  nor nor_10 (nor_10_out, X, nor_2_out);
  nor nor_11 (nor_11_out, Y, Z);
  nor nor_12 (nor_12_out, X, Z);
  nor nor_13 (nor_13_out, nor_1_out, Y);
  nor nor_14 (nor_14_out, X, Z);
  nor nor_15 (nor_15_out, Y, nor_3_out);
  nor nor_16 (dp, nor_1_out, nor_2_out, Z);
  nor nor_17 (nor_17_out, nor_4_out, nor_5_out);
  nor nor_18 (nor_18_out, nor_7_out, nor_8_out, nor_9_out);
  nor nor_19 (nor_19_out, nor_10_out, nor_11_out);
  nor nor_20 (nor_20_out, nor_12_out, nor_13_out);
  nor nor_21 (nor_21_out, nor_14_out, nor_15_out);
  nor nor_22 (a, nor_17_out, nor_17_out);
  nor nor_23 (e, nor_19_out, nor_19_out);
  nor nor_24 (f, nor_20_out, nor_20_out);
  nor nor_25 (g, nor_21_out, nor_21_out);
  nor nor_26 (c, nor_18_out, nor_18_out);
  _7_Segment_Display u_7_segment_display_1 (.g(g), .f(f), .a(a), .b(b), .e(e), .d(c), .c(c), .dp(dp));

  // Other names for the same wires on the sheet: d = c
endmodule
