// Logisim project 05 - Combinational_Part - Using_MUX.circ as structural Verilog: 1 circuit, main circuit main
module main (
  input  [1:0] Y,
  input  Z,
  input  in_3,
  input  in_4
);

  wire a, b, c, DP, e, f, g, not_1_out;

  not not_1 (not_1_out, Z);
  Multiplexer #(.select(2)) multiplexer_1 (
    .in0(not_1_out), .in1(not_1_out), .in2(in_4), .in3(Z), .out(a), .sel(Y));  // open: en
  Multiplexer #(.select(2)) multiplexer_2 (
    .in0(not_1_out), .in1(not_1_out), .in2(in_3), .in3(Z), .out(b), .sel(Y));  // open: en
  Multiplexer #(.select(2)) multiplexer_3 (
    .in0(not_1_out), .in1(in_4), .in2(in_4), .in3(Z), .out(c), .sel(Y));  // open: en
  Multiplexer #(.select(2)) multiplexer_4 (
    .in0(not_1_out), .in1(in_4), .in2(not_1_out), .in3(Z), .out(e), .sel(Y));  // open: en
  Multiplexer #(.select(2)) multiplexer_5 (
    .in0(not_1_out), .in1(not_1_out), .in2(in_4), .in3(Z), .out(f), .sel(Y));  // open: en
  Multiplexer #(.select(2)) multiplexer_6 (
    .in0(in_4), .in1(not_1_out), .in2(Z), .in3(Z), .out(g), .sel(Y));  // open: en
  Multiplexer #(.select(2)) multiplexer_7 (
    .in0(in_3), .in1(in_3), .in2(in_3), .in3(not_1_out), .out(DP), .sel(Y));  // open: en
  _7_Segment_Display u_7_segment_display_1 (.g(g), .f(f), .a(a), .b(b), .e(e), .d(c), .c(c), .dp(DP));

  // Other names for the same wires on the sheet: d = c

  // Notes on the sheet:
  //   X
endmodule
