// Logisim project 06 - Combinational_Part - Using_Decoder.circ as structural Verilog: 1 circuit, main circuit main
module main (
  input  [2:0] Z
);

  wire A, B, C, decoder_1_out0, decoder_1_out1, decoder_1_out2, decoder_1_out3, decoder_1_out4,
       decoder_1_out5, decoder_1_out7, DP, E, F, G, or_1_out, or_4_out, or_6_out, or_8_out, or_10_out;

  Decoder #(.select(3)) decoder_1 (
    .out0(decoder_1_out0), .out1(decoder_1_out1), .out2(decoder_1_out2), .out3(decoder_1_out3),
    .out4(decoder_1_out4), .out5(decoder_1_out5), .out6(DP), .out7(decoder_1_out7), .sel(Z));  // open: en
  or or_1 (or_1_out, decoder_1_out0, decoder_1_out2, decoder_1_out4);
  or or_2 (A, or_1_out, decoder_1_out5);
  or or_3 (B, decoder_1_out0, decoder_1_out2);
  or or_4 (or_4_out, decoder_1_out0, decoder_1_out2, decoder_1_out3);
  or or_5 (C, or_4_out, decoder_1_out4, decoder_1_out5);
  or or_6 (or_6_out, decoder_1_out0, decoder_1_out2, decoder_1_out3);
  or or_7 (E, or_6_out, decoder_1_out4);
  or or_8 (or_8_out, decoder_1_out0, decoder_1_out2, decoder_1_out4);
  or or_9 (F, or_8_out, decoder_1_out5);
  or or_10 (or_10_out, decoder_1_out0, decoder_1_out1, decoder_1_out2);
  or or_11 (G, or_10_out, decoder_1_out5);
  _7_Segment_Display u_7_segment_display_1 (.g(G), .f(F), .a(A), .b(B), .e(E), .d(C), .c(C), .dp(DP));

  // Other names for the same wires on the sheet: D = C

  // Notes on the sheet:
  //   X
  //   Y
endmodule
