// Logisim project Software_Implementation_Of_Project.circ as structural Verilog: 1 circuit, main circuit main
// A
module main (
  input  in_1
);

  wire A, and_1_out, B, C, clock_1_out, DP, E, F, G, j_k_ff_1_q, j_k_ff_1_qn, j_k_ff_2_q, j_k_ff_2_qn,
       j_k_ff_3_q, nand_1_out, nand_2_out, nand_3_out, nand_4_out, nand_5_out, nand_6_out, nand_7_out,
       nand_8_out, nand_9_out, nand_10_out, nand_11_out, nand_12_out, nand_13_out, nand_14_out, nand_15_out,
       nand_16_out, or_1_out, or_2_out;

  Clock clock_1 (.out(clock_1_out));
  J_K_Flip_Flop j_k_ff_1 (
    .J(and_1_out), .clk(clock_1_out), .K(j_k_ff_2_q), .Q(j_k_ff_1_q), .Qn(j_k_ff_1_qn));  // open: preset, en, reset
  J_K_Flip_Flop j_k_ff_2 (
    .J(j_k_ff_3_q), .clk(clock_1_out), .K(or_1_out), .Q(j_k_ff_2_q), .Qn(j_k_ff_2_qn));  // open: preset, en, reset
  J_K_Flip_Flop j_k_ff_3 (.J(or_2_out), .clk(clock_1_out), .K(in_1), .Q(j_k_ff_3_q));  // open: Qn, preset, en, reset
  and and_1 (and_1_out, j_k_ff_2_q, j_k_ff_3_q);
  or or_1 (or_1_out, j_k_ff_1_q, j_k_ff_3_q);
  or or_2 (or_2_out, j_k_ff_1_qn, j_k_ff_2_qn);
  nand nand_1 (nand_1_out, j_k_ff_2_q, j_k_ff_2_q);
  nand nand_2 (nand_2_out, j_k_ff_1_q, j_k_ff_1_q);
  nand nand_3 (nand_3_out, j_k_ff_3_q, j_k_ff_3_q);
  nand nand_4 (nand_4_out, nand_2_out, nand_3_out);
  nand nand_5 (nand_5_out, j_k_ff_1_q, nand_1_out);
  nand nand_6 (nand_6_out, nand_2_out, nand_3_out);
  nand nand_7 (nand_7_out, nand_2_out, j_k_ff_2_q);
  nand nand_8 (nand_8_out, j_k_ff_1_q, nand_1_out);
  nand nand_9 (nand_9_out, nand_1_out, nand_3_out);
  nand nand_10 (nand_10_out, nand_2_out, j_k_ff_2_q);
  nand nand_11 (nand_11_out, nand_1_out, nand_3_out);
  nand nand_12 (nand_12_out, nand_2_out, nand_3_out);
  nand nand_13 (nand_13_out, j_k_ff_1_q, nand_1_out);
  nand nand_14 (nand_14_out, nand_2_out, nand_3_out);
  nand nand_15 (nand_15_out, nand_1_out, j_k_ff_3_q);
  nand nand_16 (nand_16_out, j_k_ff_1_q, j_k_ff_2_q, nand_3_out);
  nand nand_17 (A, nand_4_out, nand_5_out);
  nand nand_18 (B, nand_6_out, nand_6_out);
  nand nand_19 (C, nand_7_out, nand_8_out, nand_9_out);
  nand nand_20 (E, nand_10_out, nand_11_out);
  nand nand_21 (F, nand_12_out, nand_13_out);
  nand nand_22 (G, nand_14_out, nand_15_out);
  nand nand_23 (DP, nand_16_out, nand_16_out);
  _7_Segment_Display u_7_segment_display_1 (.g(G), .f(F), .a(A), .b(B), .e(E), .d(C), .c(C), .dp(DP));

  // Other names for the same wires on the sheet: D = C

  // Notes on the sheet:
  //   "Always keep 1"
  //   Group - 02 (8-BuGS.)
endmodule
